# Fritzing sketch shield (saved by Fritzing 0.9.2b)

parts:
  Part1 = Arduino ProtoShield
  U2 = atmega328 [package=dip]
  resonator = Resonator [frequency="16 Mhz" package=THT]
  pull-up_resistor = Resistor [tolerance=±5% resistance=10k package=THT]

nets:
  5V: Part1.LED1, Part1.5V, Part1.N$94, Part1.N$113, Part1.N$175, U2.VCC, U2.AVCC, pull-up_resistor.Pin_1
  N1: Part1.D10, Part1.N$179, U2.RESET, pull-up_resistor.Pin_0
  N2: Part1.D11, Part1.N$61, U2.D11_(PWM)
  N3: Part1.D12, Part1.N$72, U2.D12
  N4: Part1.D13, Part1.N$83, U2.D13
  GND: Part1.GND, Part1.N$20, Part1.N$102, Part1.N$116, U2.GND, resonator.GND
  N5: Part1.N$5, Part1.N$80, U2.XLAT2, resonator.pin_1
  N6: Part1.N$31, Part1.N$91, U2.XLAT1, resonator.0
  N7: Part1.N$36, U2.D8
  N8: Part1.N$39, U2.D9_(PWM)
  N9: Part1.N$47, U2.D7
  N10: Part1.N$50, U2.D10_(PWM)
  N11: Part1.N$58, U2.D6_(PWM)
  N12: Part1.N$69, U2.D5_(PWM)
  N13: Part1.N$105, U2.AREF
  N14: Part1.N$124, U2.D4
  N15: Part1.N$127, U2.A0
  N16: Part1.N$135, U2.D3_(PWM)
  N17: Part1.N$138, U2.A1
  N18: Part1.N$146, U2.D2
  N19: Part1.N$149, U2.A2
  N20: Part1.N$157, U2.D1_(TX)
  N21: Part1.N$160, U2.A3
  N22: Part1.N$168, U2.D0_(RX)
  N23: Part1.N$171, U2.A4
  N24: Part1.N$182, U2.A5
